// Digital circuit RISCV_Top.dig as structural Verilog
module RISCV_Top (
  input  clk,
  input  rst,
  input  in_3
);

  wire ALUSrc, and_3_out, and_4_out, and_5_out, and_6_out, Branch, button_1_out, clk_t, comparator_1_eq,
       decoder_1_out_0, decoder_1_out_1, decoder_1_out_4, decoder_1_out_5, Jal, Jalr, MemRead, MemtoReg,
       MemWrite, not_1_out, not_2_out, not_3_out, or_2_out, RegWrite, regWrite_t, takeBranch, write_jal, Zero;
  wire [1:0] ALUOp;
  wire [2:0] funct3;
  wire [3:0] ALUControl;
  wire [6:0] funct7;
  wire [23:0] Program_Counter_q;
  wire [24:0] instr;
  wire [31:0] ALU_in2, Imm, Jalr_Adder_s, multiplexer_2_out, multiplexer_3_out, PC_branch, PC_jalr_target,
       PC_next, PC_plus4, RD1, RD2, ReadData, Result, WriteData, WriteData_from_mem;
  wire [31:24] Program_Counter_q_2;

  Button button_1 (.out(button_1_out));
  Multiplexer multiplexer_1 (.sel(in_3), .in_0(clk), .in_1(button_1_out), .out(clk_t));
  Multiplexer #(.Bits(32)) multiplexer_2 (.sel(takeBranch), .in_0(PC_plus4), .in_1(PC_branch), .out(multiplexer_2_out));
  D_FF_AS #(.Bits(32)) Program_Counter (
    .Set(1'b0), .D(PC_next), .C(clk_t), .Clr(rst), .Q({Program_Counter_q_2, Program_Counter_q}));  // open: nQ
  Comparator #(.Bits(5)) comparator_1 (.a(instr[11:7]), .b({5{1'b0}}), .eq(comparator_1_eq));  // open: gt, lt
  Multiplexer #(.Bits(32)) multiplexer_3 (
    .sel(Jal), .in_0(multiplexer_2_out), .in_1(PC_branch), .out(multiplexer_3_out));
  or or_1 (write_jal, Jal, Jalr);
  not not_1 (not_1_out, comparator_1_eq);
  and and_1 (regWrite_t, RegWrite, not_1_out);
  Multiplexer #(.Bits(32)) multiplexer_4 (.sel(Jalr), .in_0(multiplexer_3_out), .in_1(PC_jalr_target), .out(PC_next));
  Add #(.Bits(32)) PC_Adder (
    .a({Program_Counter_q_2, Program_Counter_q}), .b(32'h4), .c_i(1'b0), .s(PC_plus4));  // open: c_o
  Add #(.Bits(32)) Branch_Adder (
    .a({Program_Counter_q_2, Program_Counter_q}), .b(Imm), .c_i(1'b0), .s(PC_branch));  // open: c_o
  ROM #(.AddrBits(8), .Bits(32)) Instruction_Memory (
    .A(Program_Counter_q[9:2]), .sel(1'b1), .D({funct7, instr[24:15], funct3, instr[11:0]}));
  Add #(.Bits(32)) Jalr_Adder (.a(RD1), .b(Imm), .c_i(1'b0), .s(Jalr_Adder_s));  // open: c_o
  signExtend Sign_Extend (.instr({funct7, instr[24:15], funct3, instr[11:0]}), .opcode(instr[6:0]), .imm(Imm));
  assign PC_jalr_target = Jalr_Adder_s & 32'hfffffffe;  // And and_2, 32 bits wide
  controlUnit Control_Unit (
    .opcode(instr[6:0]), .Branch(Branch), .MemRead(MemRead), .MemtoReg(MemtoReg), .ALUOp(ALUOp),
    .MemWrite(MemWrite), .ALUSrc(ALUSrc), .RegWrite(RegWrite), .Jal(Jal), .Jalr(Jalr));  // open: LUI, AUIPC
  RegisterFile #(.AddrBits(5), .Bits(32)) Register_File (
    .Din(WriteData), .we(regWrite_t), .Rw(instr[11:7]), .C(clk_t), .Ra(instr[19:15]), .Rb(instr[24:20]),
    .Da(RD1), .Db(RD2));
  Decoder #(.Selector_Bits(3)) decoder_1 (
    .sel(funct3), .out_0(decoder_1_out_0), .out_1(decoder_1_out_1), .out_4(decoder_1_out_4),
    .out_5(decoder_1_out_5));  // open: out_2, out_3, out_6, out_7
  Multiplexer #(.Bits(32)) multiplexer_5 (.sel(ALUSrc), .in_0(RD2), .in_1(Imm), .out(ALU_in2));
  not not_2 (not_2_out, Zero);
  not not_3 (not_3_out, Result[0]);
  and and_3 (and_3_out, decoder_1_out_0, Zero);
  and and_4 (and_4_out, decoder_1_out_1, not_2_out);
  and and_5 (and_5_out, decoder_1_out_4, Result[0]);
  and and_6 (and_6_out, decoder_1_out_5, not_3_out);
  aluControl ALU_Control (.funct3(funct3), .funct7(funct7), .ALUOp(ALUOp), .ALUControl(ALUControl));
  alu ALU (.A(RD1), .B(ALU_in2), .ALUControl(ALUControl), .Zero(Zero), .Result(Result));
  or or_2 (or_2_out, and_3_out, and_4_out, and_5_out, and_6_out);
  and and_7 (takeBranch, Branch, or_2_out);
  RAMDualPort #(.AddrBits(8), .Bits(32)) Data_Memory (
    .A(Result[9:2]), .Din(RD2), .str(MemWrite), .C(clk_t), .ld(MemRead), .D(ReadData));
  Multiplexer #(.Bits(32)) multiplexer_6 (.sel(MemtoReg), .in_0(Result), .in_1(ReadData), .out(WriteData_from_mem));
  Multiplexer #(.Bits(32)) multiplexer_7 (.sel(write_jal), .in_0(WriteData_from_mem), .in_1(PC_plus4), .out(WriteData));

  // Other names for the same wires on the sheet: opcode[6:0] = instr[6:0]; rd[4:0] = instr[11:7];
  //   instr (some bits) = {funct7, funct3}; rs1[4:0] = instr[19:15]; rs2[4:0] = instr[24:20];
  //   PC_jal_target[31:0] = PC_branch; slt_result = Result[0]; WriteData_from_jal[31:0] = PC_plus4

  // Notes on the sheet:
  //   clk: Hz: 5
  //   contents of Instruction_Memory (hex, n*v repeats v):
  //   500513,200593,800613,100693,400713,700793,600393,293,313,813,2030463
  //   ,100413,2830e63,200413,4830863,300413,6830263,400413,6830c63,a000263
  //   ,a5a433,8040463,a004b3,b00533,9005b3,100813,6000a63,b62433,6040663
  //   ,b004b3,c005b3,900633,100813,4000c63,c6a433,4040863,c004b3,d00633
  //   ,9006b3,100813,2000e63,d72433,2040a63,d004b3,e006b3,900733,100813
  //   ,2000063,e7a433,40c63,e004b3,f00733,9007b3,100813,263,130313,fff38413
  //   ,40540433,8324b3,f2049ee3,80863,128293,72a433,f20412e3,63
  //   opcode
  //   funct3
  //   funct7
  //   rs1
  //   rs2
  //   rd
endmodule
